// Logisim project nibadder.circ as structural Verilog: 1 circuit, main circuit main
module main (
  input  cin,
  input  [3:0] inputA,
  input  [3:0] inputB,
  output [3:0] AplusB,
  output cout
);

  wire a0ANDb0_out, a0ANDcin_out, a1ANDb1_out, a1ANDcin_out, a2ANDb2_out, a2ANDcin_out, a3ANDb3_out,
       a3ANDcin_out, a3XORcin_out, b0ANDcin_out, b1ANDcin_out, b2ANDcin_out, b3ANDcin_out, cinXORa0_out,
       cinXORa1_out, cinXORa2_out, ORnewCin1_out, ORnewCin2_out, ORnewCin3_out;

  xor cinXORa0 (cinXORa0_out, cin, inputA[0]);
  and a0ANDb0 (a0ANDb0_out, inputA[0], inputB[0]);
  and a0ANDcin (a0ANDcin_out, cin, inputA[0]);
  and b0ANDcin (b0ANDcin_out, cin, inputB[0]);
  xor cinXORa1 (cinXORa1_out, ORnewCin1_out, inputA[1]);
  and a1ANDb1 (a1ANDb1_out, inputA[1], inputB[1]);
  and a1ANDcin (a1ANDcin_out, inputA[1], ORnewCin1_out);
  and b1ANDcin (b1ANDcin_out, inputB[1], ORnewCin1_out);
  xor cinXORa2 (cinXORa2_out, ORnewCin2_out, inputA[2]);
  and a2ANDb2 (a2ANDb2_out, inputA[2], inputB[2]);
  and a2ANDcin (a2ANDcin_out, inputA[2], ORnewCin2_out);
  and b2ANDcin (b2ANDcin_out, inputB[2], ORnewCin2_out);
  xor a3XORcin (a3XORcin_out, ORnewCin3_out, inputA[3]);
  and a3ANDb3 (a3ANDb3_out, inputA[3], inputB[3]);
  and a3ANDcin (a3ANDcin_out, inputA[3], ORnewCin3_out);
  and b3ANDcin (b3ANDcin_out, inputB[3], ORnewCin3_out);
  xor XORb0 (AplusB[0], cinXORa0_out, inputB[0]);
  xor XORb1 (AplusB[1], cinXORa1_out, inputB[1]);
  xor XORb2 (AplusB[2], cinXORa2_out, inputB[2]);
  xor XORb3 (AplusB[3], a3XORcin_out, inputB[3]);
  or ORnewCin1 (ORnewCin1_out, a0ANDb0_out, a0ANDcin_out, b0ANDcin_out);
  or ORnewCin2 (ORnewCin2_out, a1ANDb1_out, a1ANDcin_out, b1ANDcin_out);
  or ORnewCin3 (ORnewCin3_out, a2ANDb2_out, a2ANDcin_out, b2ANDcin_out);
  or ORcout (cout, a3ANDb3_out, a3ANDcin_out, b3ANDcin_out);

  // Notes on the sheet:
  //   John Graham
  //   I pledge my Honor that I have abided by the Stevens Honor System.
  //   result for first bit
  //   result for second bit
  //   result for third bit
  //   result for last bit
  //   result is carry for next bit
  //   result is carry for next bit
  //   result is carry for next bit
endmodule
