// Logisim project nibmux.circ as structural Verilog: 1 circuit, main circuit main
module main (
  input  Switch,
  input  [3:0] inputA,
  input  [3:0] inputB,
  output [3:0] AorB
);

  wire a0ANDNOTswitch_out, a1ANDNOTswitch_out, a2ANDNOTswitch_out, a3ANDNOTswitch_out, b0ANDswitch_out,
       b1ANDswitch_out, b2ANDswitch_out, b3ANDswitch_out, NOTswitch_out;

  not NOTswitch (NOTswitch_out, Switch);
  and a0ANDNOTswitch (a0ANDNOTswitch_out, inputA[0], NOTswitch_out);
  and b0ANDswitch (b0ANDswitch_out, inputB[0], Switch);
  and a1ANDNOTswitch (a1ANDNOTswitch_out, inputA[1], NOTswitch_out);
  and b1ANDswitch (b1ANDswitch_out, inputB[1], Switch);
  and a2ANDNOTswitch (a2ANDNOTswitch_out, inputA[2], NOTswitch_out);
  and b2ANDswitch (b2ANDswitch_out, inputB[2], Switch);
  and a3ANDNOTswitch (a3ANDNOTswitch_out, inputA[3], NOTswitch_out);
  and b3ANDswitch (b3ANDswitch_out, inputB[3], Switch);
  or resultBit0 (AorB[0], a0ANDNOTswitch_out, b0ANDswitch_out);
  or resultBit1 (AorB[1], a1ANDNOTswitch_out, b1ANDswitch_out);
  or resultBit2 (AorB[2], a2ANDNOTswitch_out, b2ANDswitch_out);
  or resultBit3 (AorB[3], a3ANDNOTswitch_out, b3ANDswitch_out);

  // Notes on the sheet:
  //   John Graham
  //   I pledge my honor that I have abided by the Stevens Honor System.
endmodule
