// Logisim project memories.circ as structural Verilog: 1 circuit, main circuit main
module main (
  output [7:0] memOut
);

  wire Clock1_out;
  wire [7:0] adder_1_out, PC_q;

  Register PC (.D(adder_1_out), .en(1'b1), .clk(Clock1_out), .Q(PC_q));  // open: clr
  Clock Clock1 (.out(Clock1_out));
  Adder adder_1 (.a(8'h1), .b(PC_q), .out(adder_1_out));  // open: cin, cout
  RAM mem (.addr(PC_q), .we(1'b0), .oe(1'b1), .clk(Clock1_out), .dout(memOut));  // open: din

  // Notes on the sheet:
  //   John Graham
  //   I pledge my honor that I have abided by the Stevens Honor System.
endmodule
